# Fritzing sketch daisychain_hub --xs (saved by Fritzing 0.9.3b)
circuit board: 2.33592cm x 5.11714cm
circuit board: 2.33592cm x 5.11714cm
breadboards: 1

parts:
  SparkFun_74HC4051_8-Channel_Mux_Breakout1 = SparkFun-74HC4051-8-Channel-Mux-Breakout [part_number=BOB-13906]
  Part1 = Adafruit HUZZAH32 ESP32 Feather [part_number="Adafruit #3405"]  # not connected
  J1 = Generic female header - 6 pins [form="♀ (female)" package=THT]
  J2 = female pin header, 12 pins [form="♀ (female)"]
  J3 = female pin header, 16 pins [form="♀ (female)"]
  J4 = Generic female header - 6 pins [form="♀ (female)" package=THT]
  SparkFun_74HC4051_8-Channel_Mux_Breakout2 = SparkFun-74HC4051-8-Channel-Mux-Breakout [part_number=BOB-13906]

nets:
  N1: SparkFun_74HC4051_8-Channel_Mux_Breakout1.VCC, J1.pin2
  N2: J2.pin1, SparkFun_74HC4051_8-Channel_Mux_Breakout2.Z
  N3: J2.pin2, J4.5V
  N4: J2.pin9, SparkFun_74HC4051_8-Channel_Mux_Breakout2.S0
  N5: J3.pin15, J4.pin2, SparkFun_74HC4051_8-Channel_Mux_Breakout2.VCC
  N6: J4.pin3, SparkFun_74HC4051_8-Channel_Mux_Breakout2.Y2
  N7: J4.pin4, SparkFun_74HC4051_8-Channel_Mux_Breakout2.Y1
  N8: J4.pin5, SparkFun_74HC4051_8-Channel_Mux_Breakout2.Y0

notes:
  GND
  VBATT
  3.3V
  SCL
  Z
  IO13/A12
  IO12/A11
  IO27/A10

custom parts:
  Generic female header - 6 pins: Generic female header
