# Fritzing sketch daisypair --jst (saved by Fritzing 0.9.3b)
circuit board: 3.05cm x 2.45461cm
breadboards: 1

parts:
  LSM9DS1 = SparkFun-LSM9DS1-Breakout [part_number=SEN-13284]
  IN = female pin header, 4 pins [form="♀ (female)"]
  OUT = female pin header, 4 pins [form="♀ (female)"]
  JGND = Solder Jumper [package=sj_2s-notrace]

nets:
  N1: LSM9DS1.VDD, IN.pin3, OUT.pin3
  N2: LSM9DS1.SDA, IN.pin2, OUT.pin2
  N3: LSM9DS1.SCL, IN.pin1, OUT.pin1
  N4: LSM9DS1.SDO_M, JGND.1

notes:
  GND
  VCC
  SDA
  SCL

custom parts:
  SparkFun-LSM9DS1-Breakout: The LSM9DS1 is a versatile, motion-sensing system-in-a-chip. It houses a 3-axis accelerometer, 3-axis gyroscope, and 3-axis magnetometer – nine degrees of freedom (9DOF) in a single IC! The LSM9DS1 is equipped with a digital interface, but even that is flexible: it supports both I2C and SPI, so you’ll be hard-pressed to find a microcontroller it doesn’t work with. Each sensor in the LSM9DS1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
