# Fritzing sketch daisychain --v2 (saved by Fritzing 0.9.3b)
circuit board: 2.35cm x 2.35cm
breadboards: 1

parts:
  LSM9DS1 = SparkFun-LSM9DS1-Breakout [part_number=SEN-13284]
  OUT = female pin header, 6 pins [form="♀ (female)"]
  IN = female pin header, 6 pins [form="♀ (female)"]
  SJ5 = Solder Jumper [package=sj_2s-no]
  SJ4 = Solder Jumper [package=sj_2s-no]
  SJ3 = Solder Jumper [package=sj_2s-no]
  JGND = Solder Jumper [package=sj_2s-no]

nets:
  N1: LSM9DS1.VDD, OUT.pin5, IN.pin5
  N2: LSM9DS1.SDA, SJ5.2, SJ4.2, SJ3.2
  N3: LSM9DS1.SCL, OUT.pin1, IN.pin1
  N4: LSM9DS1.SDO_M, JGND.2
  N5: OUT.pin2, IN.pin2, SJ5.1
  N6: OUT.pin3, IN.pin3, SJ4.1
  N7: OUT.pin4, IN.pin4, SJ3.1

notes:
  GND
  VCC
  SCL
  SDA2 LED
  IN
  OUT
  SDA0
  SDA1
  SDA2
  ADDRS

custom parts:
  SparkFun-LSM9DS1-Breakout: The LSM9DS1 is a versatile, motion-sensing system-in-a-chip. It houses a 3-axis accelerometer, 3-axis gyroscope, and 3-axis magnetometer – nine degrees of freedom (9DOF) in a single IC! The LSM9DS1 is equipped with a digital interface, but even that is flexible: it supports both I2C and SPI, so you’ll be hard-pressed to find a microcontroller it doesn’t work with. Each sensor in the LSM9DS1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
