# Fritzing sketch daisychain --xs --wLED (saved by Fritzing 0.9.3b)
circuit board: 2.35cm x 2.35cm
breadboards: 1

parts:
  LSM9DS1 = SparkFun-LSM9DS1-Breakout [part_number=SEN-13284]
  SJ5 = Solder Jumper [package=sj_2s-no]
  SJ4 = Solder Jumper [package=sj_2s-no]
  SJ3 = Solder Jumper [package=sj_2s-no]
  JGND = Solder Jumper [package=sj_2s-no]
  OUT = female pin header, 6 pins [form="♀ (female)"]
  IN = female pin header, 6 pins [form="♀ (female)"]
  LED1 = LED - 3mm [color="Red (633nm)" package="3 mm [THT]"]
  LED2 = LED - 3mm [color="Red (633nm)" package="3 mm [THT]"]
  SJ6 = Solder Jumper [package=sj_2s-notrace]
  SJ7 = Solder Jumper [package=sj_2s-notrace]
  LED3 = LED - 3mm [color="Red (633nm)" package="3 mm [THT]"]
  SJ8 = Solder Jumper [package=sj_2s-notrace]

nets:
  N1: LSM9DS1.VDD, OUT.pin5, IN.pin5
  N2: LSM9DS1.SDA, SJ5.1, SJ4.1, SJ3.1, LED1.cathode, LED2.cathode, LED3.cathode
  N3: LSM9DS1.SCL, OUT.pin1, IN.pin1
  N4: LSM9DS1.SDO_M, JGND.1
  N5: SJ5.2, OUT.pin2, IN.pin2
  N6: SJ4.2, OUT.pin3, IN.pin3
  N7: SJ3.2, OUT.pin4, IN.pin4
  N8: LED1.anode, SJ6.1
  N9: LED2.anode, SJ7.1
  N10: LED3.anode, SJ8.1

notes:
  GND
  VCC
  SDA1
  SCL
  SDA0
  SDA2
  LED GND
  SDA LEDs
  SDA2 LED
  IN
  OUT

custom parts:
  SparkFun-LSM9DS1-Breakout: The LSM9DS1 is a versatile, motion-sensing system-in-a-chip. It houses a 3-axis accelerometer, 3-axis gyroscope, and 3-axis magnetometer – nine degrees of freedom (9DOF) in a single IC! The LSM9DS1 is equipped with a digital interface, but even that is flexible: it supports both I2C and SPI, so you’ll be hard-pressed to find a microcontroller it doesn’t work with. Each sensor in the LSM9DS1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
