# Fritzing sketch daisychain_hub --pi (saved by Fritzing 0.9.3b)
circuit board: 3.05cm x 6.57cm
breadboards: 1

parts:
  SparkFun_74HC4051_8-Channel_Mux_Breakout2 = SparkFun-74HC4051-8-Channel-Mux-Breakout [part_number=BOB-13906]  # not connected
  MCU1 = Raspberry Pi Zero  # not connected
  J6 = double row female pin header, 40 pins [form="♀ (female)"]
  J8 = female pin header, 11 pins [form="♀ (female)"]
  J7 = female pin header, 8 pins [form="♀ (female)"]
  J5 = female pin header, 6 pins [form="♀ (female)"]
  J10 = double row female pin header, 6 pins [form="♀ (female)"]
  J11 = double row female pin header, 6 pins [form="♀ (female)"]
  J9 = double row female pin header, 4 pins [form="♀ (female)"]
  J12 = double row female pin header, 6 pins [form="♀ (female)"]

nets:
  N1: J6.pin12, J7.pin7
  N2: J6.pin13, J7.pin6
  N3: J6.pin16, J9.pin1
  N4: J6.pin17, J9.pin4
  N5: J6.pin19, J12.pin4, J12.pin5, J12.pin6
  N6: J6.pin21, J8.pin2, J7.pin2, J5.pin2, J10.pin4, J10.pin5, J10.pin6, J9.pin3
  N7: J6.pin22, J7.pin4, J11.pin4, J11.pin5, J11.pin6
  N8: J6.pin23, J5.pin6, J11.pin1, J11.pin2, J11.pin3
  N9: J6.pin28, J7.pin5
  N10: J8.pin4, J5.pin5
  N11: J8.pin5, J5.pin4
  N12: J8.pin6, J5.pin3
  N13: J10.pin1, J10.pin2, J10.pin3, J12.pin1, J12.pin2, J12.pin3

notes:
  SCL
  SDA0
  SDA1
  SDA2
  SDA
  23
  S1
  22
  24
  S2
  S0
  Z
  3.3V
  VCC
  GND
  LOCAR Pi Wing v.1.0
  TX
  RX
  SERIAL COM
  MULTIPLEXER
  5V
  AUX
  OUT
