# Fritzing sketch daisyhub --v3 (saved by Fritzing 0.9.3b)
circuit board: 2.35cm x 2.35cm
breadboards: 1

parts:
  LSM9DS1 = SparkFun-LSM9DS1-Breakout [part_number=SEN-13284]
  IN = double row female pin header, 10 pins [form="♀ (female)"]
  OUT = double row female pin header, 10 pins [form="♀ (female)"]  # not connected
  SJ1 = Solder Jumper [package=sj_2s-notrace]
  SJ2 = Solder Jumper [package=sj_2s-notrace]
  SJ3 = Solder Jumper [package=sj_2s-notrace]
  SJ6 = Solder Jumper [package=sj_2s-notrace]
  SJ7 = Solder Jumper [package=sj_2s-notrace]
  SJ5 = Solder Jumper [package=sj_2s-no]
  SJ4 = Solder Jumper [package=sj_2s-no]

nets:
  N1: LSM9DS1.VDD, IN.pin5
  N2: LSM9DS1.SDA, SJ1.1, SJ2.1, SJ5.1
  N3: LSM9DS1.SCL, IN.pin1
  N4: IN.pin2, SJ6.2
  N5: IN.pin3, SJ4.2
  N6: IN.pin4, SJ7.2
  N7: IN.pin7, SJ3.2
  N8: IN.pin8, SJ2.2
  N9: IN.pin9, SJ1.2
  N10: IN.pin10, SJ5.2

notes:
  SDA2 LED
  IN
  OUT

custom parts:
  SparkFun-LSM9DS1-Breakout: The LSM9DS1 is a versatile, motion-sensing system-in-a-chip. It houses a 3-axis accelerometer, 3-axis gyroscope, and 3-axis magnetometer – nine degrees of freedom (9DOF) in a single IC! The LSM9DS1 is equipped with a digital interface, but even that is flexible: it supports both I2C and SPI, so you’ll be hard-pressed to find a microcontroller it doesn’t work with. Each sensor in the LSM9DS1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
