# Fritzing sketch psupply --v1 (saved by Fritzing 0.9.3b)
circuit board: 3.02814cm x 5.27166cm
breadboards: 1

parts:
  part = ATX24 Pin Power Supply Connector [package=atx24_right_angle]
  part_2 = female pin header, 5 pins [form="♀ (female)"]
  part_3 = female pin header, 5 pins [form="♀ (female)"]
  part_4 = female pin header, 5 pins [form="♀ (female)"]
  part_5 = female pin header, 5 pins [form="♀ (female)"]
  part_6 = female pin header, 5 pins [form="♀ (female)"]
  part_7 = female pin header, 5 pins [form="♀ (female)"]
  part_8 = double row female pin header, 24 pins [form="♀ (female)"]

nets:
  N1: part.3.3V, part_2.pin1, part_2.pin2, part_2.pin3, part_2.pin4, part_2.pin5, part_8.pin1, part_8.pin2, part_8.pin3, part_8.pin22, part_8.pin23, part_8.pin24
  N2: part.GND, part.PS_ON
  N3: part.5V, part_4.pin1, part_4.pin2, part_4.pin3, part_4.pin4, part_4.pin5, part_8.pin4, part_8.pin5, part_8.pin6, part_8.pin19, part_8.pin20, part_8.pin21
  N4: part.PWR_OK, part_8.pin15
  N5: part.5V_STDBY, part_8.pin11, part_8.pin12, part_8.pin13, part_8.pin14
  N6: part.12V, part_6.pin1, part_6.pin2, part_6.pin3, part_6.pin4, part_6.pin5, part_8.pin7, part_8.pin8, part_8.pin9, part_8.pin16, part_8.pin17, part_8.pin18
  N7: part.NC, part_8.pin10
  N8: part_3.pin1, part_3.pin2, part_3.pin3, part_3.pin4, part_3.pin5
  N9: part_5.pin1, part_5.pin2, part_5.pin3, part_5.pin4, part_5.pin5
  N10: part_7.pin1, part_7.pin2, part_7.pin3, part_7.pin4, part_7.pin5

notes:
  3.3v
  12v
  5v
  PWR_OK
  5v_SB
  NC
  GND
